// Digital circuit hw3_d.dig as structural Verilog
module hw3_d (
  input  [3:0] X,
  input  [3:0] Y,
  output [3:0] Z
);

  wire comparator_1_gt, multiplexer_1_out;

  Multiplexer multiplexer_1 (.sel(comparator_1_gt), .in_0(1'b1), .in_1(1'b0), .out(multiplexer_1_out));
  Comparator #(.Bits(4)) comparator_1 (.a(X), .b(Y), .gt(comparator_1_gt));  // open: eq, lt
  Add #(.Bits(4)) add_1 (.a(X), .b(4'b0101), .c_i(multiplexer_1_out), .s(Z));  // open: c_o
endmodule
